# Fritzing sketch console (saved by Fritzing 0.9.3b)

parts:
  U1 = AUDIO-JACK2 [package=audio-jack]
  SP1 = SPEAKER [package=pcb_mount_speaker]
  SP2 = SPEAKER [package=pcb_mount_speaker]
  Raspberry_Pi_1 = Raspberry Pi 3 [part_number=RPI-3-V1.2]  # not connected
  Part2 = TRRS 3.5mm Jack Breakout
  Part3 = PowerBoost 1000 Basic
  U2 = LIPO-2000mAh [package=lipo-2000]  # not connected
  S1 = SPST Switch [package=switch-spdt-smd]
  LED2 = RGB LED (com. anode, rbg) [package="5 mm [THT]"]
  R2 = Resistor [tolerance=±5% resistance=10k package="2010 [SMD]"]
  R3 = Resistor [tolerance=±5% resistance=100 package="2010 [SMD]"]

nets:
  N1: U1.RING, SP1.+, SP2.+, Part2.SLEEVE
  N2: U1.RSH, Part2.RING1
  N3: U1.SLEEVE, SP1.-
  N4: U1.TIP, SP2.-
  N5: U1.TSH, Part2.TIP
  N6: Part3.GND, S1.O, R2.Pin_0, R3.Pin_0
  N7: Part3.ENABLE, Part3.LBO, S1.S
  N8: Part3.5.0V, S1.P, LED2.common_anode

custom parts:
  PowerBoost 1000 Basic: The PowerBoost 1000 is a little DC/DC boost converter module that can run from 1.8V batteries or higher, and convert the battery output to 5.2V DC for running your 5V projects. At its heart is a TPS61030 boost converter from TI. This boost converter chip has some really nice extras such as low battery detection, 4A internal switch, synchronous conversion, excellent efficiency, and 700KHz high-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
