# Fritzing sketch duinocon (saved by Fritzing 0.9.3b)
perfboards: 6

parts:
  Part1 = Arduino Micro (Rev3)
  Part3 = PowerBoost 1000 Basic
  U1 = SWITCH_SPDT [package=kps-1290]
  LED1 = RGB LED (com. anode, rbg) [package="5 mm [THT]"]
  Part4 = Thumb Joystick
  Part5 = Thumb Joystick
  R1 = Resistor [tolerance=±5% resistance=10k package="2010 [SMD]"]
  R2 = Resistor [tolerance=±5% resistance=100 package="2010 [SMD]"]
  S3 = Pushbutton [package="[SMD]"]
  S4 = Pushbutton [package="[SMD]"]
  S5 = Pushbutton [package="[SMD]"]
  S6 = Pushbutton [package="[SMD]"]
  U2 = 74HC595 [package="DIP16 [THT]"]
  S7 = Pushbutton [package="[SMD]"]
  R3 = Resistor [tolerance=±5% resistance=10k package=THT]
  R4 = Resistor [tolerance=±5% resistance=10k package=THT]
  R5 = Resistor [tolerance=±5% resistance=10k package=THT]
  R6 = Resistor [tolerance=±5% resistance=10k package=THT]
  R7 = Resistor [tolerance=±5% resistance=10k package=THT]
  S8 = Pushbutton [package="[SMD]"]
  S9 = Pushbutton [package="[SMD]"]
  R8 = Resistor [tolerance=±5% resistance=10k package=THT]
  R9 = Resistor [tolerance=±5% resistance=10k package=THT]
  S10 = Pushbutton [package="[SMD]"]
  U3 = 74HC595 [package="DIP16 [THT]"]
  S11 = Pushbutton [package="[SMD]"]
  S12 = Pushbutton [package="[SMD]"]
  S13 = Pushbutton [package="[SMD]"]
  S14 = Pushbutton [package="[SMD]"]
  R10 = Resistor [tolerance=±5% resistance=10k package=THT]
  R11 = Resistor [tolerance=±5% resistance=10k package=THT]
  R12 = Resistor [tolerance=±5% resistance=10k package=THT]
  R13 = Resistor [tolerance=±5% resistance=10k package=THT]
  R14 = Resistor [tolerance=±5% resistance=10k package=THT]
  S15 = Pushbutton [package="[SMD]"]
  S16 = Pushbutton [package="[SMD]"]
  R15 = Resistor [tolerance=±5% resistance=10k package=THT]
  R16 = Resistor [tolerance=±5% resistance=10k package=THT]

nets:
  N1: Part1.D2/SDA, U2.Q1, U3.Q1
  N2: Part1.D3/SCL, U2.Q0, U3.Q0
  N3: Part1.D4_PWM/A6, U2.Q7'
  N4: Part1.D5_PWM, U2.Q2, U3.Q2
  VCC: Part1.5V, Part3.5.0V, U1.S, Part4.VCC, Part5.VCC, S5.Pin_1, S5.Pin_2, U2.VCC, S7.Pin_1, S7.Pin_2, S8.Pin_1, S8.Pin_2, S9.Pin_1, S9.Pin_2, S10.Pin_1, S10.Pin_2, U3.VCC, S11.Pin_3, S11.Pin_4, S12.Pin_1, S12.Pin_2, S13.Pin_1, S13.Pin_2, S14.Pin_3, S14.Pin_4, S15.Pin_1, S15.Pin_2, S16.Pin_1, S16.Pin_2
  GND: Part3.GND, Part4.GND, U3.GND, R11.Pin_0, R12.Pin_1, R13.Pin_0, R14.Pin_1
  N5: Part3.ENABLE, U1.P
  N6: Part3.LBO, R2.Pin_0
  GND_2: U1.O, Part5.GND, R1.Pin_0, U2.GND, R3.Pin_1, R4.Pin_0, R5.Pin_1, R6.Pin_1, R7.Pin_0
  N7: LED1.red_cathode, R2.Pin_1
  N8: LED1.blue_cathode, R1.Pin_1
  N9: Part4.SEL, U3.Q6
  N10: Part5.SEL, U2.Q3
  N11: S3.Pin_1, S3.Pin_2
  N12: S3.Pin_3, S3.Pin_4, U2.ST_CP, R6.Pin_0
  N13: S4.Pin_1, S4.Pin_2
  N14: S4.Pin_3, S4.Pin_4, U2.OE, R5.Pin_0
  N15: S5.Pin_3, S5.Pin_4, U2.SH_CP, R7.Pin_1
  N16: S6.Pin_1, S6.Pin_2
  N17: S6.Pin_3, S6.Pin_4, U2.DS, R4.Pin_1
  N18: U2.Q4, S9.Pin_3, S9.Pin_4, R9.Pin_1
  N19: U2.Q5, S8.Pin_3, S8.Pin_4, R8.Pin_1
  N20: U2.Q6, S7.Pin_3, S7.Pin_4, R3.Pin_0
  N21: U2.MR, U3.Q7'
  N22: R8.Pin_0, R9.Pin_0
  N23: S10.Pin_3, S10.Pin_4, U3.Q3, R10.Pin_0
  N24: U3.Q4, S15.Pin_3, S15.Pin_4, R15.Pin_1
  N25: U3.Q5, S16.Pin_3, S16.Pin_4, R16.Pin_1
  N26: U3.SH_CP, S12.Pin_3, S12.Pin_4, R13.Pin_1
  N27: U3.ST_CP, S14.Pin_1, S14.Pin_2, R11.Pin_1
  N28: U3.OE, S13.Pin_3, S13.Pin_4, R12.Pin_0
  N29: U3.DS, S11.Pin_1, S11.Pin_2, R14.Pin_0
  N30: R15.Pin_0, R16.Pin_0

notes:
  Opposite sides of same board

custom parts:
  PowerBoost 1000 Basic: The PowerBoost 1000 is a little DC/DC boost converter module that can run from 1.8V batteries or higher, and convert the battery output to 5.2V DC for running your 5V projects. At its heart is a TPS61030 boost converter from TI. This boost converter chip has some really nice extras such as low battery detection, 4A internal switch, synchronous conversion, excellent efficiency, and 700KHz high-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
